# Fritzing sketch scheme (saved by Fritzing 1.0.8)
breadboards: 2

parts:
  A1 = ESP32 DevKitc V4
  Componente1 = LCD1602-I2C
  Componente2 = I2C level shifter bidirectional
  LED1 = 7-SEGMENT-4DIGIT-YOUNGSUN [package=7-segment-4digit-youngsun-longpads]
  U2 = 74HC595 [package="DIP16 [THT]"]
  DI1 = 7 Segment Display
  R1 = Resistor [tolerance=±5% resistance=220 package="2512 [SMD]"]
  R2 = Resistor [tolerance=±5% resistance=220 package="2512 [SMD]"]
  R3 = Resistor [tolerance=±5% resistance=220 package="2512 [SMD]"]
  R4 = Resistor [tolerance=±5% resistance=220 package="2512 [SMD]"]
  R5 = Resistor [tolerance=±5% resistance=220 package="2512 [SMD]"]
  R6 = Resistor [tolerance=±5% resistance=220 package="2512 [SMD]"]
  R7 = Resistor [tolerance=±5% resistance=220 package="2512 [SMD]"]
  R8 = Resistor [tolerance=±5% resistance=220 package="2512 [SMD]"]
  R9 = Resistor [tolerance=±5% resistance=1000 package="2512 [SMD]"]
  R10 = Resistor [tolerance=±5% resistance=1000 package="2512 [SMD]"]
  R11 = Resistor [tolerance=±5% resistance=1000 package="2512 [SMD]"]
  R12 = Resistor [tolerance=±5% resistance=1000 package="2512 [SMD]"]
  R13 = Resistor [tolerance=±5% resistance=1000 package="2512 [SMD]"]
  Q1 = NPN-Transistor [package="TO92 [THT]"]
  Q2 = NPN-Transistor [package="TO92 [THT]"]
  Q3 = NPN-Transistor [package="TO92 [THT]"]
  Q4 = NPN-Transistor [package="TO92 [THT]"]
  Q5 = NPN-Transistor [package="TO92 [THT]"]
  C1 = Capacitor Polarized [package=cpol-radial-100uf-25v]
  S1 = Pushbutton [package="[THT]"]
  S2 = Pushbutton [package="[THT]"]
  S3 = Pushbutton [package="[THT]"]
  S4 = Pushbutton [package="[THT]"]
  S5 = Pushbutton [package="[THT]"]
  S6 = Pushbutton [package="[THT]"]
  S7 = Pushbutton [package="[THT]"]
  S8 = Pushbutton [package="[THT]"]
  S9 = Pushbutton [package="[THT]"]
  S10 = Pushbutton [package="[THT]"]
  S11 = Pushbutton [package="[THT]"]
  S12 = Pushbutton [package="[THT]"]
  R14 = Resistor [tolerance=±5% power=0.25W resistance=10k package=THT]
  R15 = Resistor [tolerance=±5% power=0.25W resistance=10k package=THT]
  R16 = Resistor [tolerance=±5% power=0.25W resistance=10k package=THT]
  R17 = Resistor [tolerance=±5% power=0.25W resistance=10k package=THT]
  RE1 = KY-040 Rotary encoder [package="Breakout board"]

nets:
  VCC: A1.Pin_1, Componente2.LV, U2.MR, U2.VCC, RE1.Vcc
  N1: A1.Pin_2, C1.+
  N2: A1.Pin_3, S1.Pin_3, S1.Pin_4, S5.Pin_3, S5.Pin_4, S9.Pin_3, S9.Pin_4
  N3: A1.Pin_4, S2.Pin_3, S2.Pin_4, S7.Pin_3, S7.Pin_4, S11.Pin_3, S11.Pin_4
  N4: A1.Pin_5, S3.Pin_3, S3.Pin_4, S6.Pin_3, S6.Pin_4, S10.Pin_3, S10.Pin_4
  N5: A1.Pin_6, S4.Pin_3, S4.Pin_4, S8.Pin_3, S8.Pin_4, S12.Pin_3, S12.Pin_4
  N6: A1.Pin_8, RE1.SW
  N7: A1.Pin_9, U2.ST_CP
  N8: A1.Pin_10, U2.SH_CP
  N9: A1.Pin_11, U2.DS
  N10: A1.Pin_12, S1.Pin_1, S1.Pin_2, S2.Pin_1, S2.Pin_2, S3.Pin_1, S3.Pin_2, S4.Pin_1, S4.Pin_2
  N11: A1.Pin_13, S5.Pin_1, S6.Pin_1, S6.Pin_2, S7.Pin_1, S7.Pin_2, S8.Pin_1, S8.Pin_2
  GND: A1.Pin_14, A1.Pin_32, A1.Pin_38, Componente1.GND, Componente2.GND, U2.GND, U2.OE, Q1.E, Q2.E, Q3.E, Q4.E, Q5.E, C1.-, R14.Pin_1, R15.Pin_1, R16.Pin_1, R17.Pin_1, RE1.GND
  N12: A1.Pin_15, S9.Pin_1, S10.Pin_1, S10.Pin_2, S11.Pin_1, S11.Pin_2, S12.Pin_1, S12.Pin_2
  N13: A1.Pin_19, Componente1.VCC, Componente2.HV
  N14: A1.Pin_26, R10.Pin_0
  N15: A1.Pin_27, R9.Pin_0
  N16: A1.Pin_28, R11.Pin_0
  N17: A1.Pin_29, R12.Pin_0
  N18: A1.Pin_30, R13.Pin_0
  N19: A1.Pin_31, RE1.DT
  N20: A1.Pin_33, Componente2.LV2
  N21: A1.Pin_36, Componente2.LV1
  N22: A1.Pin_37, RE1.CLK
  N23: Componente1.SDA, Componente2.HV2
  N24: Componente1.SCL, Componente2.HV1
  N25: LED1.DIG1, Q1.B
  N26: LED1.DIG2, Q2.B
  N27: LED1.D, DI1.Segment_D, R5.Pin_0
  N28: LED1.E, DI1.Segment_E, R4.Pin_0
  N29: LED1.DIG3, Q3.B
  N30: LED1.DP, DI1.Segment_DP, R1.Pin_0
  N31: LED1.DIG4, Q4.B
  N32: LED1.F, DI1.Segment_F, R3.Pin_0
  N33: LED1.C, DI1.Segment_C, R7.Pin_0
  N34: LED1.A, DI1.Segment_A, R8.Pin_0
  N35: LED1.G, DI1.Segment_G, R2.Pin_0
  N36: LED1.B, DI1.Segment_B, R6.Pin_0
  N37: U2.Q1, R6.Pin_1
  N38: U2.Q2, R7.Pin_1
  N39: U2.Q3, R5.Pin_1
  N40: U2.Q4, R4.Pin_1
  N41: U2.Q5, R3.Pin_1
  N42: U2.Q6, R2.Pin_1
  N43: U2.Q7, R1.Pin_1
  N44: U2.Q0, R8.Pin_1
  N45: DI1.common_cathode, Q5.B
  N46: R9.Pin_1, Q1.C
  N47: R10.Pin_1, Q2.C
  N48: R11.Pin_1, Q3.C
  N49: R12.Pin_1, Q4.C
  N50: R13.Pin_1, Q5.C

custom parts:
  ESP32 DevKitc V4: ESP32-DevKitC board with ESP32-WROOM-32 module. ESP32-DevKitC V4 is a small-sized ESP32-based development board produced by Espressif. Most of the pins on the ESP module are broken out to the pin headers on the board. The pins D0, D1, D2, D3, CMD and CLK are used internally for communication between ESP32 and SPI flash memory. They are grouped on both sides near the USB connector. Avoid using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
  LCD1602-I2C: A standard character display, usually with 2x16 characters. Comes in many colors with LCM1602 IIC attached.
  KY-040 Rotary encoder: KY-040 Rotary Encoder with switch on breakout borad from AZ Delivery
